// Logisim project circuit.circ as structural Verilog: 7 circuits, main circuit pin_slice
module pin_slice (
  input  zi,
  input  ci,
  input  qi,
  input  wi,
  output wo,
  output co,
  output qo,
  output zo
);

  wire and_1_out;

  D_Flip_Flop d_ff_1 (.clk(ci), .D(qi), .Q(qo));  // open: Qn, preset, en, reset
  or or_1 (zo, zi, and_1_out);
  and and_1 (and_1_out, qo, wi);

  assign co = ci;
  assign wo = wi;
endmodule

module pin (
  input  PSI,
  input  W0,
  input  W1,
  input  W2,
  output Z0,
  output Z1,
  output Z2
);

  wire PCLK_out, pin_slice_1_co, pin_slice_1_qo, pin_slice_1_zo, pin_slice_2_co, pin_slice_2_qo,
       pin_slice_2_wo, pin_slice_2_zo, pin_slice_3_co, pin_slice_3_qo, pin_slice_3_wo, pin_slice_3_zo,
       pin_slice_5_co, pin_slice_5_qo, pin_slice_5_zo, pin_slice_6_co, pin_slice_6_qo, pin_slice_6_wo,
       pin_slice_7_co, pin_slice_7_qo, pin_slice_7_wo, pin_slice_7_zo, pin_slice_8_co, pin_slice_8_qo,
       pin_slice_8_wo, pin_slice_9_co, pin_slice_9_qo, pin_slice_9_wo, pin_slice_9_zo;

  Button PCLK (.out(PCLK_out));
  pin_slice pin_slice_1 (
    .ci(pin_slice_6_co), .qi(pin_slice_6_qo), .zo(pin_slice_1_zo), .wi(pin_slice_2_wo), .zi(1'b0),
    .co(pin_slice_1_co), .qo(pin_slice_1_qo));  // open: wo
  pin_slice pin_slice_2 (
    .ci(pin_slice_8_co), .qi(pin_slice_8_qo), .zo(pin_slice_2_zo), .wi(pin_slice_3_wo), .zi(1'b0),
    .co(pin_slice_2_co), .qo(pin_slice_2_qo), .wo(pin_slice_2_wo));
  pin_slice pin_slice_3 (
    .ci(PCLK_out), .qi(PSI), .zo(pin_slice_3_zo), .wi(W0), .zi(1'b0), .co(pin_slice_3_co),
    .qo(pin_slice_3_qo), .wo(pin_slice_3_wo));
  pin_slice pin_slice_4 (
    .ci(pin_slice_5_co), .qi(pin_slice_5_qo), .zo(Z0), .wi(pin_slice_6_wo), .zi(pin_slice_5_zo));  // open: co, qo, wo
  pin_slice pin_slice_5 (
    .ci(pin_slice_1_co), .qi(pin_slice_1_qo), .zo(pin_slice_5_zo), .wi(pin_slice_7_wo), .zi(pin_slice_1_zo),
    .co(pin_slice_5_co), .qo(pin_slice_5_qo));  // open: wo
  pin_slice pin_slice_6 (
    .ci(pin_slice_7_co), .qi(pin_slice_7_qo), .zo(Z1), .wi(pin_slice_8_wo), .zi(pin_slice_7_zo),
    .co(pin_slice_6_co), .qo(pin_slice_6_qo), .wo(pin_slice_6_wo));
  pin_slice pin_slice_7 (
    .ci(pin_slice_2_co), .qi(pin_slice_2_qo), .zo(pin_slice_7_zo), .wi(pin_slice_9_wo), .zi(pin_slice_2_zo),
    .co(pin_slice_7_co), .qo(pin_slice_7_qo), .wo(pin_slice_7_wo));
  pin_slice pin_slice_8 (
    .ci(pin_slice_9_co), .qi(pin_slice_9_qo), .zo(Z2), .wi(W2), .zi(pin_slice_9_zo), .co(pin_slice_8_co),
    .qo(pin_slice_8_qo), .wo(pin_slice_8_wo));
  pin_slice pin_slice_9 (
    .ci(pin_slice_3_co), .qi(pin_slice_3_qo), .zo(pin_slice_9_zo), .wi(W1), .zi(pin_slice_3_zo),
    .co(pin_slice_9_co), .qo(pin_slice_9_qo), .wo(pin_slice_9_wo));
endmodule

module pin_slice_flipped (
  input  zi,
  input  clk,
  input  qi,
  input  wi,
  output wo,
  output clk_o,
  output qo,
  output zo
);

  wire and_1_out;

  D_Flip_Flop d_ff_1 (.clk(clk), .D(qi), .Q(qo));  // open: Qn, preset, en, reset
  or or_1 (zo, zi, and_1_out);
  and and_1 (and_1_out, qo, wi);

  assign clk_o = clk;
  assign wo = wi;
endmodule

module shift_slice (
  input  SCLKI,
  input  Z,
  input  LDI,
  input  SI,
  output SCLKO,
  output LDO,
  output SO
);

  wire and_1_out, and_2_out, not_1_out, or_1_out;

  not not_1 (not_1_out, LDI);
  and and_1 (and_1_out, Z, not_1_out);
  or or_1 (or_1_out, and_1_out, and_2_out);
  and and_2 (and_2_out, LDI, SI);
  D_Flip_Flop d_ff_1 (.clk(SCLKI), .D(or_1_out), .Q(SO));  // open: Qn, preset, en, reset

  assign LDO = LDI;
  assign SCLKO = SCLKI;
endmodule

module shift (
  input  SI,
  input  LD,
  input  Z0,
  input  Z1,
  input  Z2,
  output SO
);

  wire SCLK_out, shift_slice_1_ldo, shift_slice_1_sclko, shift_slice_1_so, shift_slice_2_ldo,
       shift_slice_2_sclko, shift_slice_2_so;

  Button SCLK (.out(SCLK_out));
  shift_slice shift_slice_1 (
    .SCLKI(SCLK_out), .Z(Z0), .LDI(LD), .SI(SI), .SO(shift_slice_1_so), .SCLKO(shift_slice_1_sclko),
    .LDO(shift_slice_1_ldo));
  shift_slice shift_slice_2 (
    .SCLKI(shift_slice_1_sclko), .Z(Z1), .LDI(shift_slice_1_ldo), .SI(shift_slice_1_so),
    .SO(shift_slice_2_so), .SCLKO(shift_slice_2_sclko), .LDO(shift_slice_2_ldo));
  shift_slice shift_slice_3 (
    .SCLKI(shift_slice_2_sclko), .Z(Z2), .LDI(shift_slice_2_ldo), .SI(shift_slice_2_so), .SCLKO(SO));  // open: SO, LDO
endmodule

module top (
  input  PSI,
  input  SI,
  input  LD,
  output SO
);

  wire PCLK_out, pin_slice_1_co, pin_slice_1_qo, pin_slice_1_zo, pin_slice_2_co, pin_slice_2_qo,
       pin_slice_2_wo, pin_slice_2_zo, pin_slice_3_co, pin_slice_3_qo, pin_slice_3_wo, pin_slice_3_zo,
       pin_slice_4_co, pin_slice_4_qo, pin_slice_4_zo, pin_slice_5_co, pin_slice_5_qo, pin_slice_5_wo,
       pin_slice_5_zo, pin_slice_6_co, pin_slice_6_qo, pin_slice_6_wo, pin_slice_6_zo, pin_slice_7_zo,
       pin_slice_8_co, pin_slice_8_qo, pin_slice_8_wo, pin_slice_8_zo, pin_slice_9_co, pin_slice_9_qo,
       pin_slice_9_wo, pin_slice_9_zo, SCLK_out, shift_slice_1_ldo, shift_slice_1_sclko, shift_slice_1_so,
       shift_slice_2_ldo, shift_slice_2_sclko, shift_slice_2_so, shift_slice_3_so;

  Button PCLK (.out(PCLK_out));
  Button SCLK (.out(SCLK_out));
  pin_slice pin_slice_1 (
    .ci(pin_slice_8_co), .qi(pin_slice_8_qo), .zo(pin_slice_1_zo), .wi(pin_slice_2_wo), .zi(1'b0),
    .co(pin_slice_1_co), .qo(pin_slice_1_qo));  // open: wo
  pin_slice pin_slice_2 (
    .ci(pin_slice_9_co), .qi(pin_slice_9_qo), .zo(pin_slice_2_zo), .wi(pin_slice_3_wo), .zi(1'b0),
    .co(pin_slice_2_co), .qo(pin_slice_2_qo), .wo(pin_slice_2_wo));
  pin_slice pin_slice_3 (
    .ci(PCLK_out), .qi(PSI), .zo(pin_slice_3_zo), .wi(shift_slice_1_so), .zi(1'b0), .co(pin_slice_3_co),
    .qo(pin_slice_3_qo), .wo(pin_slice_3_wo));
  shift_slice shift_slice_1 (
    .SCLKI(SCLK_out), .Z(pin_slice_7_zo), .LDI(LD), .SI(SI), .SO(shift_slice_1_so),
    .SCLKO(shift_slice_1_sclko), .LDO(shift_slice_1_ldo));
  pin_slice pin_slice_4 (
    .ci(pin_slice_1_co), .qi(pin_slice_1_qo), .zo(pin_slice_4_zo), .wi(pin_slice_5_wo), .zi(pin_slice_1_zo),
    .co(pin_slice_4_co), .qo(pin_slice_4_qo));  // open: wo
  pin_slice pin_slice_5 (
    .ci(pin_slice_2_co), .qi(pin_slice_2_qo), .zo(pin_slice_5_zo), .wi(pin_slice_6_wo), .zi(pin_slice_2_zo),
    .co(pin_slice_5_co), .qo(pin_slice_5_qo), .wo(pin_slice_5_wo));
  pin_slice pin_slice_6 (
    .ci(pin_slice_3_co), .qi(pin_slice_3_qo), .zo(pin_slice_6_zo), .wi(shift_slice_2_so),
    .zi(pin_slice_3_zo), .co(pin_slice_6_co), .qo(pin_slice_6_qo), .wo(pin_slice_6_wo));
  shift_slice shift_slice_2 (
    .SCLKI(shift_slice_1_sclko), .Z(pin_slice_8_zo), .LDI(shift_slice_1_ldo), .SI(shift_slice_1_so),
    .SO(shift_slice_2_so), .SCLKO(shift_slice_2_sclko), .LDO(shift_slice_2_ldo));
  pin_slice pin_slice_7 (
    .ci(pin_slice_4_co), .qi(pin_slice_4_qo), .zo(pin_slice_7_zo), .wi(pin_slice_8_wo), .zi(pin_slice_4_zo));  // open: co, qo, wo
  pin_slice pin_slice_8 (
    .ci(pin_slice_5_co), .qi(pin_slice_5_qo), .zo(pin_slice_8_zo), .wi(pin_slice_9_wo), .zi(pin_slice_5_zo),
    .co(pin_slice_8_co), .qo(pin_slice_8_qo), .wo(pin_slice_8_wo));
  pin_slice pin_slice_9 (
    .ci(pin_slice_6_co), .qi(pin_slice_6_qo), .zo(pin_slice_9_zo), .wi(shift_slice_3_so),
    .zi(pin_slice_6_zo), .co(pin_slice_9_co), .qo(pin_slice_9_qo), .wo(pin_slice_9_wo));
  shift_slice shift_slice_3 (
    .SCLKI(shift_slice_2_sclko), .Z(pin_slice_9_zo), .LDI(shift_slice_2_ldo), .SI(shift_slice_2_so),
    .SO(shift_slice_3_so), .SCLKO(SO));  // open: LDO
endmodule

module shift_slice_mux (
  input  SCLKI,
  input  LDI,
  input  Z,
  input  SI,
  output SCLKO,
  output LDO,
  output SO
);

  wire multiplexer_1_out;

  Multiplexer #(.disabled(0), .enable("false")) multiplexer_1 (.in0(Z), .in1(SI), .out(multiplexer_1_out), .sel(LDI));
  D_Flip_Flop d_ff_1 (.clk(SCLKI), .D(multiplexer_1_out), .Q(SO));  // open: Qn, preset, en, reset

  assign LDO = LDI;
  assign SCLKO = SCLKI;
endmodule
